# Fritzing sketch schematic (saved by Fritzing 0.8.5b)
breadboards: 1

parts:
  IC1 = SO-28W [chip_label=atmega168 package=SO(w)]
  LED1 = LED - 5mm [color="Red (633nm)" package="5 mm [THT]"]
  R1 = Resistor [tolerance=±5% resistance=220 package=THT]
  R2 = Resistor [tolerance=±5% resistance=10k package=THT]
  S1 = Pushbutton [package=THT]
  R3 = Resistor [tolerance=±5% resistance=10k package=THT]
  IC2 = IC, DIP package, 10 pins [chip_label=ISP]

nets:
  N1: IC1.1, R3.Pin_1, IC2.pin5
  5V: IC1.7, IC1.20, S1.leg0, R3.Pin_0
  GND: IC1.8, IC1.22, R1.Pin_1, R2.Pin_1, IC2.pin8, IC2.pin10
  N2: IC1.14, LED1.anode
  N3: IC1.15, R2.Pin_0, S1.leg1
  N4: IC1.17, IC2.pin1
  N5: IC1.18, IC2.pin9
  N6: IC1.19, IC2.pin7
  N7: LED1.cathode, R1.Pin_0
